// Logisim project CSIRAC.circ as structural Verilog: 7 circuits, main circuit main
module main (
  input  [4:0] in_1,
  input  Write,
  input  Reset
);

  wire flexowriter_printer_1_ready, p6of32_1_p_6, p13of32_1_p_13;
  wire [4:0] flexowriter_printer_1_data, splitgroups_1_group3, splitgroups_1_group4;
  wire [11:0] rom_1_data;
  wire [15:0] Program_Tape_tapeaddress;
  wire [19:0] ChainUnit_q;
  wire [31:0] P3_Source_selectors;

  ROM #(.addrWidth(16), .dataWidth(12)) rom_1 (.addr(Program_Tape_tapeaddress), .data(rom_1_data));
  Program_Tape_Reader Program_Tape (
    .TapeData(rom_1_data), .TapeAddress(Program_Tape_tapeaddress));  // open: Reset, ReadNext, Overflow, Ready, Data
  Flexowriter_Printer flexowriter_printer_1 (
    .Enable(1'b1), .Clock(Write), .Reset(Reset), .Char(in_1), .Data(flexowriter_printer_1_data),
    .Ready(flexowriter_printer_1_ready));
  Chain_Unit ChainUnit (.Q(ChainUnit_q));  // open: D, Clock
  SplitGroups splitgroups_1 (
    .Word(ChainUnit_q), .Group3(splitgroups_1_group3), .Group4(splitgroups_1_group4));  // open: Group1, Group2
  // Probe on splitgroups_1_group3
  // Probe on splitgroups_1_group4
  Unit_Selector P3_Source (.Opcode(splitgroups_1_group3), .Enable(1'b1), .Selectors(P3_Source_selectors));
  Unit_Selector P4_Destination (.Opcode(splitgroups_1_group4), .Enable(1'b1));  // open: Selectors
  P6of32 p6of32_1 (.Plugs(P3_Source_selectors), .P_6(p6of32_1_p_6));
  P13of32 p13of32_1 (.Plugs(P3_Source_selectors), .P_13(p13of32_1_p_13));
  // Probe on p6of32_1_p_6
  // Probe on p13of32_1_p_13
  // LedBar #(.inputtype("row"), .matrixcols(5)) ledbar_1: pin names not known; wires that end beside it: flexowriter_printer_1_data
  LED led_1 (.in(flexowriter_printer_1_ready));
endmodule

module Unit_Selector (
  input  [4:0] Opcode,
  input  Enable,
  output [31:0] Selectors
);

  wire not_1_out, not_2_out, not_3_out, not_4_out, not_5_out, V17a_out, V17b_out, V18a_out, V18b_out,
       V19a_out, V19b_out, V20a_out, V20b_out, V21a_out, V21b_out, V22a_out, V22b_out, V23a_out, V23b_out,
       V24a_out, V24b_out, V25a_out, V25b_out, V26a_out, V26b_out, V27a_out, V27b_out, V28a_out, V28b_out,
       V29a_out, V29b_out, V30a_out, V30b_out, V31a_out, V31b_out, V37a_out, V37b_out;

  not not_1 (not_1_out, Opcode[4]);
  not not_2 (not_2_out, Opcode[3]);
  not not_3 (not_3_out, Opcode[2]);
  not not_4 (not_4_out, Opcode[1]);
  not not_5 (not_5_out, Opcode[0]);
  and V24b (V24b_out, Opcode[1], Enable);
  and V24a (V24a_out, not_4_out, Enable);
  and V37b (V37b_out, Enable, not_5_out);
  and V37a (V37a_out, Opcode[0], Enable);
  and V28b (V28b_out, Opcode[2], V24b_out);
  and V28a (V28a_out, V24b_out, not_3_out);
  and V20b (V20b_out, V24a_out, Opcode[2]);
  and V20a (V20a_out, V24a_out, not_3_out);
  and V30b (V30b_out, Opcode[3], V28b_out);
  and V30a (V30a_out, not_2_out, V28b_out);
  and V26b (V26b_out, Opcode[3], V28a_out);
  and V26a (V26a_out, not_2_out, V28a_out);
  and V22b (V22b_out, Opcode[3], V20b_out);
  and V22a (V22a_out, not_2_out, V20b_out);
  and V18b (V18b_out, V20a_out, Opcode[3]);
  and V18a (V18a_out, V20a_out, not_2_out);
  and V31b (V31b_out, Opcode[4], V30b_out);
  and V31a (V31a_out, V30b_out, not_1_out);
  and V29b (V29b_out, Opcode[4], V30a_out);
  and V29a (V29a_out, V30a_out, not_1_out);
  and V27b (V27b_out, Opcode[4], V26b_out);
  and V27a (V27a_out, V26b_out, not_1_out);
  and V25b (V25b_out, Opcode[4], V26a_out);
  and V25a (V25a_out, V26a_out, not_1_out);
  and V23b (V23b_out, Opcode[4], V22b_out);
  and V23a (V23a_out, V22b_out, not_1_out);
  and V21b (V21b_out, Opcode[4], V22a_out);
  and V21a (V21a_out, V22a_out, not_1_out);
  and V19b (V19b_out, Opcode[4], V18b_out);
  and V19a (V19a_out, V18b_out, not_1_out);
  and V17b (V17b_out, Opcode[4], V18a_out);
  and V17a (V17a_out, V18a_out, not_1_out);
  and V15b (Selectors[29], V37b_out, V31b_out);
  and V15a (Selectors[28], V31b_out, V37a_out);
  and V16b (Selectors[31], V37b_out, V31a_out);
  and V16a (Selectors[30], V31a_out, V37a_out);
  and V13b (Selectors[25], V37b_out, V29b_out);
  and V13a (Selectors[24], V29b_out, V37a_out);
  and V14b (Selectors[27], V37b_out, V29a_out);
  and V14a (Selectors[26], V29a_out, V37a_out);
  and V11b (Selectors[21], V37b_out, V27b_out);
  and V11a (Selectors[20], V27b_out, V37a_out);
  and V12b (Selectors[23], V37b_out, V27a_out);
  and V12a (Selectors[22], V27a_out, V37a_out);
  and V9b (Selectors[17], V37b_out, V25b_out);
  and V9a (Selectors[16], V25b_out, V37a_out);
  and V10b (Selectors[19], V37b_out, V25a_out);
  and V10a (Selectors[18], V25a_out, V37a_out);
  and V7b (Selectors[13], V37b_out, V23b_out);
  and V7a (Selectors[12], V23b_out, V37a_out);
  and V8b (Selectors[15], V37b_out, V23a_out);
  and V8a (Selectors[14], V23a_out, V37a_out);
  and V5b (Selectors[9], V37b_out, V21b_out);
  and V5a (Selectors[8], V21b_out, V37a_out);
  and V6b (Selectors[11], V37b_out, V21a_out);
  and V6a (Selectors[10], V21a_out, V37a_out);
  and V3b (Selectors[5], V37b_out, V19b_out);
  and V3a (Selectors[4], V19b_out, V37a_out);
  and V4b (Selectors[7], V37b_out, V19a_out);
  and V4a (Selectors[6], V19a_out, V37a_out);
  and V1b (Selectors[1], V37b_out, V17b_out);
  and V1a (Selectors[0], V17b_out, V37a_out);
  and V2b (Selectors[3], V37b_out, V17a_out);
  and V2a (Selectors[2], V17a_out, V37a_out);
  // Probe on Selectors[29]
  // Probe on Selectors[28]
  // Probe on Selectors[31]
  // Probe on Selectors[30]
  // Probe on Selectors[25]
  // Probe on Selectors[24]
  // Probe on Selectors[27]
  // Probe on Selectors[26]
  // Probe on Selectors[21]
  // Probe on Selectors[20]
  // Probe on Selectors[23]
  // Probe on Selectors[22]
  // Probe on Selectors[17]
  // Probe on Selectors[16]
  // Probe on Selectors[19]
  // Probe on Selectors[18]
  // Probe on Selectors[13]
  // Probe on Selectors[12]
  // Probe on Selectors[15]
  // Probe on Selectors[14]
  // Probe on Selectors[9]
  // Probe on Selectors[8]
  // Probe on Selectors[11]
  // Probe on Selectors[10]
  // Probe on Selectors[5]
  // Probe on Selectors[4]
  // Probe on Selectors[7]
  // Probe on Selectors[6]
  // Probe on Selectors[1]
  // Probe on Selectors[0]
  // Probe on Selectors[3]
  // Probe on Selectors[2]

  // Notes on the sheet:
  //   Enable is usually P2_3
  //   E
  //   D
  //   F
  //   C
  //   G
  //   B
  //   H
  //   A
  //   J
  //   I
  //   Map input opcode to plug number for source or destination
  //   N0 to N31 are the decoded opcode numbers
endmodule

// SIPO
module Chain_Unit (
  input  D,
  input  Clock,
  output [19:0] Q
);

  wire not_1_out, V1_q, V1_qn, V2_q, V2_qn, V3_q, V3_qn, V4_q, V4_qn, V5_q, V5_qn, V6_q, V6_qn, V7_q, V7_qn,
       V8_q, V8_qn, V9_q, V9_qn, V10_q, V10_qn, V11_q, V11_qn, V12_q, V12_qn, V13_q, V13_qn, V14_q, V14_qn,
       V15_q, V15_qn, V16_q, V16_qn, V17_q, V17_qn, V18_q, V18_qn, V19_q, V19_qn, V20_q, V20_qn;

  not not_1 (not_1_out, D);
  S_R_Flip_Flop V1 (.S(D), .R(not_1_out), .clk(Clock), .Q(V1_q), .Qn(V1_qn));  // open: reset, preset
  S_R_Flip_Flop V6 (.S(V5_q), .R(V5_qn), .clk(Clock), .Q(V6_q), .Qn(V6_qn));  // open: reset, preset
  S_R_Flip_Flop V11 (.S(V10_q), .R(V10_qn), .clk(Clock), .Q(V11_q), .Qn(V11_qn));  // open: reset, preset
  S_R_Flip_Flop V16 (.S(V15_q), .R(V15_qn), .clk(Clock), .Q(V16_q), .Qn(V16_qn));  // open: reset, preset
  S_R_Flip_Flop V2 (.S(V1_q), .R(V1_qn), .clk(Clock), .Q(V2_q), .Qn(V2_qn));  // open: reset, preset
  S_R_Flip_Flop V7 (.S(V6_q), .R(V6_qn), .clk(Clock), .Q(V7_q), .Qn(V7_qn));  // open: reset, preset
  S_R_Flip_Flop V12 (.S(V11_q), .R(V11_qn), .clk(Clock), .Q(V12_q), .Qn(V12_qn));  // open: reset, preset
  S_R_Flip_Flop V17 (.S(V16_q), .R(V16_qn), .clk(Clock), .Q(V17_q), .Qn(V17_qn));  // open: reset, preset
  buf buffer_1 (Q[0], V1_q);
  buf buffer_2 (Q[5], V6_q);
  buf buffer_3 (Q[10], V11_q);
  buf buffer_4 (Q[15], V16_q);
  buf buffer_5 (Q[1], V2_q);
  S_R_Flip_Flop V3 (.S(V2_q), .R(V2_qn), .clk(Clock), .Q(V3_q), .Qn(V3_qn));  // open: reset, preset
  S_R_Flip_Flop V8 (.S(V7_q), .R(V7_qn), .clk(Clock), .Q(V8_q), .Qn(V8_qn));  // open: reset, preset
  S_R_Flip_Flop V13 (.S(V12_q), .R(V12_qn), .clk(Clock), .Q(V13_q), .Qn(V13_qn));  // open: reset, preset
  S_R_Flip_Flop V18 (.S(V17_q), .R(V17_qn), .clk(Clock), .Q(V18_q), .Qn(V18_qn));  // open: reset, preset
  buf buffer_6 (Q[6], V7_q);
  buf buffer_7 (Q[11], V12_q);
  buf buffer_8 (Q[16], V17_q);
  buf buffer_9 (Q[2], V3_q);
  S_R_Flip_Flop V4 (.S(V3_q), .R(V3_qn), .clk(Clock), .Q(V4_q), .Qn(V4_qn));  // open: reset, preset
  buf buffer_10 (Q[7], V8_q);
  S_R_Flip_Flop V9 (.S(V8_q), .R(V8_qn), .clk(Clock), .Q(V9_q), .Qn(V9_qn));  // open: reset, preset
  buf buffer_11 (Q[12], V13_q);
  S_R_Flip_Flop V14 (.S(V13_q), .R(V13_qn), .clk(Clock), .Q(V14_q), .Qn(V14_qn));  // open: reset, preset
  buf buffer_12 (Q[17], V18_q);
  S_R_Flip_Flop V19 (.S(V18_q), .R(V18_qn), .clk(Clock), .Q(V19_q), .Qn(V19_qn));  // open: reset, preset
  S_R_Flip_Flop V5 (.S(V4_q), .R(V4_qn), .clk(Clock), .Q(V5_q), .Qn(V5_qn));  // open: reset, preset
  S_R_Flip_Flop V10 (.S(V9_q), .R(V9_qn), .clk(Clock), .Q(V10_q), .Qn(V10_qn));  // open: reset, preset
  S_R_Flip_Flop V15 (.S(V14_q), .R(V14_qn), .clk(Clock), .Q(V15_q), .Qn(V15_qn));  // open: reset, preset
  S_R_Flip_Flop V20 (.S(V19_q), .R(V19_qn), .clk(Clock), .Q(V20_q), .Qn(V20_qn));  // open: reset, preset
  buf buffer_13 (Q[3], V4_q);
  buf buffer_14 (Q[8], V9_q);
  buf buffer_15 (Q[13], V14_q);
  buf buffer_16 (Q[18], V19_q);
  buf buffer_17 (Q[4], V5_q);
  buf buffer_18 (Q[9], V10_q);
  buf buffer_19 (Q[14], V15_q);
  buf buffer_20 (Q[19], V20_q);
  // Probe on V20_q
  // Probe on V20_qn

  // Notes on the sheet:
  //   P8
  //   P11
  //   Chain Unit - 20-bit shift register.
  //   Also includes the buffering from the Chain Output schematic.
endmodule

module Flexowriter_Printer (
  input  [4:0] Char,
  input  Enable,
  input  Clock,
  input  Reset,
  output [4:0] Data,
  output Ready
);

  wire and_1_out, and_2_out, comparator_1_eq, comparator_2_eq, d_ff_1_q, d_ff_1_qn, nor_1_out, not_1_out,
       or_1_out;
  wire [5:5] sr_latch_2_q;
  wire [6:0] CharGen_data;

  and and_1 (and_1_out, Clock, Enable);
  not not_1 (not_1_out, Clock);
  Register #(.width(5)) register_1 (.D(Char), .en(Enable), .clk(Clock), .Q(Data), .clr(Reset));
  D_Flip_Flop d_ff_1 (.D(1'b1), .clk(and_1_out), .Q(d_ff_1_q), .Qn(d_ff_1_qn), .reset(not_1_out));  // open: preset
  TTY #(.cols(80)) tty_1 (.data(CharGen_data), .clk(not_1_out), .we(and_2_out), .clr(Reset));
  and and_2 (and_2_out, nor_1_out, d_ff_1_q);
  Comparator #(.mode("unsigned"), .width(5)) comparator_1 (
    .a(5'b11011), .b(Data), .eq(comparator_1_eq));  // open: gt, lt
  Comparator #(.mode("unsigned"), .width(5)) comparator_2 (
    .a(5'b11110), .b(Data), .eq(comparator_2_eq));  // open: gt, lt
  SR_Latch sr_latch_1 (.Set(d_ff_1_qn), .Reset(and_1_out), .Q(Ready));  // open: nQ
  ROM #(.addrWidth(6), .dataWidth(7)) CharGen (.addr({sr_latch_2_q[5], Data}), .data(CharGen_data));
  or or_1 (or_1_out, comparator_2_eq, Reset);
  nor nor_1 (nor_1_out, comparator_2_eq, comparator_2_eq);
  SR_Latch sr_latch_2 (.Set(comparator_1_eq), .Reset(or_1_out), .Q(sr_latch_2_q[5]));  // open: nQ

  // Notes on the sheet:
  //   Output to 5-hole tape punch
  //   Figure Shift?
  //   Letter Shift?
  //   contents of CharGen (hex, n*v repeats v):
  //   5f 51 57 43 52 4b 4c 55 49 44 56 41 46 4d 47 4e 50 4a 48 45 42 54 59 53 58 4f 5a e 20 a f 8 5f 31 32
  //   2a 34 28 29 37 38 23 3d 2d 26 2e 9 2c 30 73 24 33 27 35 36 2f 78 39 2b e 20 a f 8
  //   Leading edge of Ready
  //   indicates punch Data is valid.
endmodule

module Program_Tape_Reader (
  input  Reset,
  input  [11:0] TapeData,
  input  ReadNext,
  output Overflow,
  output [15:0] TapeAddress,
  output [19:0] Data,
  output Ready
);

  wire not_1_out, not_2_out;
  wire [15:0] undriven;

  // NoConnect on undriven
  not not_1 (not_1_out, ReadNext);
  Counter #(.max('hffff), .width(16)) counter_1 (
    .clr(Reset), .load(1'b0), .up(1'b1), .count(1'b1), .clk(not_1_out), .D(undriven), .carry(Overflow),
    .Q(TapeAddress));
  Register #(.width(12)) register_1 (
    .D(TapeData), .en(1'b1), .clk(ReadNext), .Q({Data[19:18], Data[9:0]}), .clr(Reset));
  not not_2 (not_2_out, ReadNext);
  D_Flip_Flop d_ff_1 (.D(1'b1), .clk(not_2_out), .Q(Ready), .reset(ReadNext));  // open: Qn, preset

  assign Data[17:10] = {8{1'b0}};

  // Notes on the sheet:
  //   Up to 64K words of 12-hole program tape data which is provided
  //   by a RAM or ROM block in the parent circuit.
  //   Convert 12-hole punch tape
  //   data into 20-bit words.
endmodule

module Interpreter (
  input  [19:0] P15,
  input  Enable,
  input  Clear,
  output [4:0] SrcOp,
  output [4:0] DestOp
);

  wire p1of20_1_p_1, p2of20_1_p_2, p3of20_1_p_3, p4of20_1_p_4, p5of20_1_p_5, p6of20_1_p_6, p7of20_1_p_7,
       p8of20_1_p_8, p9of20_1_p_9, p10of20_1_p_10, V33_out, V35_out, V37_out, V39_out, V41_out, V43_out,
       V45_out, V47_out, V49_out, V51_out;

  P10of20 p10of20_1 (.Plugs(P15), .P_10(p10of20_1_p_10));
  P9of20 p9of20_1 (.Plugs(P15), .P_9(p9of20_1_p_9));
  P8of20 p8of20_1 (.Plugs(P15), .P_8(p8of20_1_p_8));
  P7of20 p7of20_1 (.Plugs(P15), .P_7(p7of20_1_p_7));
  P6of20 p6of20_1 (.Plugs(P15), .P_6(p6of20_1_p_6));
  and V33 (V33_out, p10of20_1_p_10, Enable);
  and V35 (V35_out, p9of20_1_p_9, Enable);
  and V37 (V37_out, p8of20_1_p_8, Enable);
  and V39 (V39_out, p7of20_1_p_7, Enable);
  and V41 (V41_out, p6of20_1_p_6, Enable);
  SR_Latch V34 (.Set(V33_out), .Reset(Clear), .Q(SrcOp[4]));  // open: nQ
  SR_Latch V36 (.Set(V35_out), .Reset(Clear), .Q(SrcOp[3]));  // open: nQ
  SR_Latch V38 (.Set(V37_out), .Reset(Clear), .Q(SrcOp[2]));  // open: nQ
  SR_Latch V40 (.Set(V39_out), .Reset(Clear), .Q(SrcOp[1]));  // open: nQ
  SR_Latch V42 (.Set(V41_out), .Reset(Clear), .Q(SrcOp[0]));  // open: nQ
  P5of20 p5of20_1 (.Plugs(P15), .P_5(p5of20_1_p_5));
  P4of20 p4of20_1 (.Plugs(P15), .P_4(p4of20_1_p_4));
  P3of20 p3of20_1 (.Plugs(P15), .P_3(p3of20_1_p_3));
  P2of20 p2of20_1 (.Plugs(P15), .P_2(p2of20_1_p_2));
  P1of20 p1of20_1 (.Plugs(P15), .P_1(p1of20_1_p_1));
  and V43 (V43_out, p5of20_1_p_5, Enable);
  and V45 (V45_out, p4of20_1_p_4, Enable);
  and V47 (V47_out, p3of20_1_p_3, Enable);
  and V49 (V49_out, p2of20_1_p_2, Enable);
  and V51 (V51_out, p1of20_1_p_1, Enable);
  SR_Latch V44 (.Set(V43_out), .Reset(Clear), .Q(DestOp[4]));  // open: nQ
  SR_Latch V46 (.Set(V45_out), .Reset(Clear), .Q(DestOp[3]));  // open: nQ
  SR_Latch V48 (.Set(V47_out), .Reset(Clear), .Q(DestOp[2]));  // open: nQ
  SR_Latch V50 (.Set(V49_out), .Reset(Clear), .Q(DestOp[1]));  // open: nQ
  SR_Latch V52 (.Set(V51_out), .Reset(Clear), .Q(DestOp[0]));  // open: nQ
endmodule

// SR
module SR_Latch (
  input  Set,
  input  Reset,
  output nQ,
  output Q
);

  wire and_1_out, not_1_out;

  not not_1 (not_1_out, Reset);
  and and_1 (and_1_out, Set, not_1_out);
  nor nor_1 (nQ, and_1_out, Q);
  nor nor_2 (Q, nQ, Reset);

  // Notes on the sheet:
  //   Safe SR latch that doesn't malfunction with S = R = 1
endmodule
